# Fritzing sketch PDI EXT3 Messages Particle (saved by Fritzing 0.9.3b)
circuit board: 5.68414cm x 4.00097cm

parts:
  J2 = shrouded pin header, 20 pins [form="♂ (shrouded male)"]
  Composant1 = Photon

nets:
  3.3V: J2.pin1, Composant1.3V3
  SCK: J2.pin2, Composant1.A3
  BUSY: J2.pin3, Composant1.D5
  D/C: J2.pin4, Composant1.D4
  Panel /RESET: J2.pin5, Composant1.D3
  MISO: J2.pin6, Composant1.A4
  MOSI: J2.pin7, Composant1.A5
  Flash /CS: J2.pin8, Composant1.D2
  Panel /CS: J2.pin9, Composant1.D1
  GND: J2.pin10, Composant1.GND

notes:
  +3.3V
  GROUND
  Panel /CS
  PDI EXT3 Messages Particle, Rei Vilo 2021 - CC BY SA NC, 2
